# Fritzing sketch Electronics Project 2 (saved by Fritzing 1.0.7)

parts:
  PDH1 = rev_pdh  # not connected
  cntl1 = roborio_v2
  BAT1 = Battery 12V [package=battcom_20mm_pth]
  CB1 = Thermal Circuit Breaker [package=waterproof]
  JP2 = APP SB50 [package=sb50]
  JP3 = APP SB50 [package=sb50]
  Mod1 = VRM
  FRC1 = Vivid Hosting FRC Radio
  BLDC3 = CTRE Falcon 500 [part_number=19-708850]
  RSL1 = FRC Robot Signal Light [part_number=855PB-B12ME522]
  PDH2 = rev_pdh
  FRC6 = 10A Circuit Breaker
  FRC7 = 10A Circuit Breaker
  FRC8 = 10A Circuit Breaker
  FRC9 = 10A Circuit Breaker
  CANcoder1 = CTRE CANcoder [package=THT]
  BLDC4 = CTRE Falcon 500 [part_number=19-708850]
  BLDC5 = CTRE Falcon 500 [part_number=19-708850]
  BLDC6 = CTRE Falcon 500 [part_number=19-708850]
  BLDC7 = CTRE Falcon 500 [part_number=19-708850]
  BLDC8 = CTRE Falcon 500 [part_number=19-708850]
  BLDC9 = CTRE Falcon 500 [part_number=19-708850]
  BLDC11 = CTRE Falcon 500 [part_number=19-708850]
  CANcoder2 = CTRE CANcoder [package=THT]
  CANcoder3 = CTRE CANcoder [package=THT]
  CANcoder4 = CTRE CANcoder [package=THT]
  Pigeon_2_1 = CTRE Pigeon 2.0 [package=THT]
  Part1 = 3 Port Wago Connector
  Part2 = 3 Port Wago Connector
  Part3 = 3 Port Wago Connector
  Part4 = 3 Port Wago Connector
  R1 = Resistor [tolerance=±5% power=0.25W resistance=120 package=THT]
  CANivore1 = CTRE CANivore [form="♀ (female)" package=THT]
  BLDC12 = CTRE Falcon 500 [part_number=19-708850]
  BLDC13 = CTRE Falcon 500 [part_number=19-708850]
  BLDC14 = CTRE Falcon 500 [part_number=19-708850]
  BLDC15 = CTRE Falcon 500 [part_number=19-708850]
  FRC10 = 10A Circuit Breaker
  FRC11 = 10A Circuit Breaker
  FRC12 = 10A Circuit Breaker
  FRC13 = 10A Circuit Breaker  # not connected
  FRC14 = 10A Circuit Breaker
  FRC15 = 10A Circuit Breaker
  FRC16 = 10A Circuit Breaker
  FRC17 = 10A Circuit Breaker
  FRC18 = 10A Circuit Breaker
  FRC19 = 10A Circuit Breaker  # not connected
  R2 = Resistor [tolerance=±5% power=0.25W resistance=120 package=THT]

nets:
  N1: cntl1.connector0, BLDC3.CANL0
  N2: cntl1.connector1, BLDC3.CANH1#3
  N3: cntl1.connector39, PDH2.connector49
  N4: cntl1.connector40, PDH2.connector48
  N5: cntl1.connector41, RSL1.anode0, RSL1.anode1
  N6: cntl1.connector42, RSL1.common_cathode
  N7: cntl1.connector142, CANivore1.USB-C
  N8: cntl1.connector144, FRC1.RIO
  N9: BAT1.+, JP3.2
  N10: BAT1.-, JP3.1
  N11: CB1.1, PDH2.connector45
  N12: CB1.2, JP2.2
  N13: JP2.1, PDH2.connector44
  N14: Mod1.5V_2A_GND0, Mod1.5V_500mA_GND1, Mod1.12V_2A_GND0, Mod1.12V_2A_GND1, Mod1.12V_500mA_GND0, Mod1.12V_500mA_GND1, Mod1.InGnd, FRC1.12V_-, PDH2.connector46, CANcoder1.+, CANcoder2.-, CANcoder3.-, CANcoder4.+, Pigeon_2_1.-, Part2.port1, Part2.port2, Part2.port3, Part4.port1, Part4.port2, Part4.port3, CANivore1.V-[B]
  N15: Mod1.12V_2A_12v0, FRC1.12V_+
  N16: Mod1.12V_2A_12v1, CANivore1.V+[R]
  N17: Mod1.12V_500mA_12v0, CANcoder1.-, CANcoder4.-, Pigeon_2_1.+, Part3.port1, Part3.port2, Part3.port3
  N18: Mod1.12V_500mA_12v1, CANcoder2.+, CANcoder3.+, Part1.port1, Part1.port2, Part1.port3
  N19: Mod1.In12V, PDH2.connector47
  N20: BLDC3.Vin-, PDH2.connector19
  N21: BLDC3.Vin+, PDH2.connector18
  N22: BLDC3.CANL1, BLDC4.CANL0
  N23: BLDC3.CANH1#5, BLDC4.CANH1#3
  N24: PDH2.connector4, BLDC11.Vin+
  N25: PDH2.connector5, BLDC11.Vin-
  N26: PDH2.connector6, BLDC9.Vin+
  N27: PDH2.connector7, BLDC9.Vin-
  N28: PDH2.connector8, BLDC8.Vin+
  N29: PDH2.connector9, BLDC8.Vin-
  N30: PDH2.connector10, BLDC7.Vin+
  N31: PDH2.connector11, BLDC7.Vin-
  N32: PDH2.connector12, BLDC6.Vin+
  N33: PDH2.connector13, BLDC6.Vin-
  N34: PDH2.connector14, BLDC5.Vin+
  N35: PDH2.connector15, BLDC5.Vin-
  N36: PDH2.connector16, BLDC4.Vin+
  N37: PDH2.connector17, BLDC4.Vin-
  N38: PDH2.connector20, BLDC15.Vin+
  N39: PDH2.connector21, BLDC15.Vin-
  N40: PDH2.connector22, BLDC12.Vin+
  N41: PDH2.connector23, BLDC12.Vin-
  N42: PDH2.connector24, BLDC13.Vin+
  N43: PDH2.connector25, BLDC13.Vin-
  N44: PDH2.connector26, BLDC14.Vin-
  N45: PDH2.connector27, BLDC14.Vin+
  N46: PDH2.connector54, FRC6.1
  N47: PDH2.connector55, FRC6.2
  N48: PDH2.connector56, FRC7.1
  N49: PDH2.connector57, FRC7.2
  N50: PDH2.connector59, FRC16.2
  N51: PDH2.connector60, FRC10.1
  N52: PDH2.connector61, FRC10.2
  N53: PDH2.connector62, FRC17.1
  N54: PDH2.connector63, FRC17.2
  N55: PDH2.connector64, FRC11.1
  N56: PDH2.connector65, FRC11.2
  N57: PDH2.connector66, FRC18.1
  N58: PDH2.connector67, FRC18.2
  N59: PDH2.connector72, FRC12.1
  N60: PDH2.connector73, FRC12.2
  N61: PDH2.connector80, FRC15.1
  N62: PDH2.connector81, FRC15.2
  N63: PDH2.connector84, FRC14.1
  N64: PDH2.connector85, FRC14.2
  N65: PDH2.connector94, FRC8.1
  N66: PDH2.connector95, FRC8.2
  N67: PDH2.connector96, FRC9.1
  N68: PDH2.connector97, FRC9.2
  N69: CANcoder1.IN-CANH[Y], CANcoder4.OUT-CANH[Y]
  N70: CANcoder1.IN-CANL[G], CANcoder4.OUT-CANL[G]
  N71: CANcoder1.OUT-CANH[Y], Pigeon_2_1.IN-CANH[Y]
  N72: CANcoder1.OUT-CANL[G], Pigeon_2_1.IN-CANL[G]
  N73: BLDC4.CANL1, BLDC5.CANL0
  N74: BLDC4.CANH1#5, BLDC5.CANH1#3
  N75: BLDC5.CANL1, BLDC6.CANL0
  N76: BLDC5.CANH1#5, BLDC6.CANH1#3
  N77: BLDC6.CANL1, BLDC7.CANL0
  N78: BLDC6.CANH1#5, BLDC7.CANH1#3
  N79: BLDC7.CANL1, BLDC8.CANL0
  N80: BLDC7.CANH1#5, BLDC8.CANH1#3
  N81: BLDC8.CANL1, BLDC9.CANL0
  N82: BLDC8.CANH1#5, BLDC9.CANH1#3
  N83: BLDC9.CANL1, BLDC11.CANL0
  N84: BLDC9.CANH1#5, BLDC11.CANH1#3
  N85: BLDC11.CANL1, CANcoder2.IN-CANL[G]
  N86: BLDC11.CANH1#5, CANcoder2.IN-CANH[Y]
  N87: CANcoder2.OUT-CANH[Y], CANcoder3.IN-CANH[Y]
  N88: CANcoder2.OUT-CANL[G], CANcoder3.IN-CANL[G]
  N89: CANcoder3.OUT-CANH[Y], CANcoder4.IN-CANH[Y]
  N90: CANcoder3.OUT-CANL[G], CANcoder4.IN-CANL[G]
  N91: Pigeon_2_1.OUT-CANH[Y], R1.Pin_1
  N92: Pigeon_2_1.OUT-CANL[G], R1.Pin_0
  N93: CANivore1.CANL[G], BLDC15.CANL0
  N94: CANivore1.CANH[Y], BLDC15.CANH1#3
  N95: BLDC12.CANL0, BLDC15.CANL1
  N96: BLDC12.CANH1#3, BLDC15.CANH1#5
  N97: BLDC12.CANL1, BLDC13.CANL0
  N98: BLDC12.CANH1#5, BLDC13.CANH1#3
  N99: BLDC13.CANL1, BLDC14.CANL0
  N100: BLDC13.CANH1#5, BLDC14.CANH1#3
  N101: BLDC14.CANL1, R2.Pin_1
  N102: BLDC14.CANH1#5, R2.Pin_0

custom parts:
  Battery 12V: Battery Holders Various common sizes : AA, AAA, 20mm coin cell and 12mm coin cell.
  Thermal Circuit Breaker: Cooper Bussman P/N CB185-120, CB185F-120, CB285-120 CB285F-120, CB285120F or Optifuse P/N 153120, 253120
  APP SB50: Anderson Power Products SB®50 Connectors feature a one-piece plastic housing using stainless steel springs to hold low-resistance contacts in place. These connectors work with wire contacts up to 6AWG (10mm²) as well as PCB and busbar contacts. The genderless design mates with itself and has a plated through-hole mounting style. Anderson SB®50 Connectors are UL-rated for hot plugging up to 50A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
  CTRE Falcon 500: The Falcon 500 powered by Talon FX is a brushless motor with an integrated motor controller and high-resolution encoder, custom designed specifically for the FIRST Robotics Competition, through a collaboration between Cross the Road Electronics and VEX Robotics.
  FRC Robot Signal Light: Panel Mount Beacon,12V AC/DC,45 mm Panel Mounting LED,Amber,22.5 mm Round Mounting Hole Used as: R709 *ROBOTS must have a signal light. ROBOTS must use at least 1, but no more than 2, diagnostic ROBOT Signal Light (RSL) (P/N 855PB-B12ME522). Any RSL must be: A. mounted on the ROBOT such that it is easily visible while standing 3 ft. (~ 100 cm) in front of the ROBOT, B. connected to the “RSL”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
  CTRE Pigeon 2.0: Generic single row SMD female header
  3 Port Wago Connector: 3 Port Wago 221 Connector
